// Digital circuit lab04.dig as structural Verilog
module lab04 (
  input  clk,
  input  rst,
  output [31:0] PC,
  output [5:0] opcode,
  output [4:0] src1__addr,
  output [31:0] src1__out,
  output [4:0] src2__addr,
  output [31:0] src2__out,
  output [4:0] dst__addr,
  output [31:0] dst__data
);

  wire ALUsrc, and_1_out, branch, Mem2Reg, MemRead, MemWrite, RegDst, RegWrite, zero;
  wire [1:0] ALUop;
  wire [1:1] undriven;
  wire [3:0] u_alu_control_alu_control;
  wire [15:0] cpumemory_d2;
  wire [31:0] _1D, ALUresult, multiplexer_1_out, multiplexer_3_out, SignExt, u_alu_2_result, u_alu_result;

  gen_register #(.applicationType("IVERILOG"), .CodeFile(".\\gen_register.v")) u_gen_register (
    .clk(clk), .rst(rst), .write_en(clk), .data_in(multiplexer_1_out), .data_out(PC));
  alu #(.applicationType("IVERILOG"), .CodeFile(".\\alu.v")) u_alu (
    .alu_control(4'b0010), .A(PC), .B(32'h4), .result(u_alu_result));  // open: zero
  RAMDualAccess #(.AddrBits(8), .isProgramMemory("true"), .Bits(32)) cpumemory (
    .str(MemWrite), .C(clk), .ld(MemRead), .A1(ALUresult[7:0]), .Din1(src2__out), .A2(PC[9:2]), .D1(_1D),
    .D2({opcode, src1__addr, src2__addr, cpumemory_d2}));
  alu #(.applicationType("IVERILOG"), .CodeFile(".\\alu.v")) u_alu_2 (
    .alu_control(4'b0010), .A(u_alu_result), .B({SignExt[31:2], undriven[1], 1'b0}), .result(u_alu_2_result));  // open: zero
  and and_1 (and_1_out, branch, zero);
  Multiplexer #(.Bits(32)) multiplexer_1 (
    .sel(and_1_out), .in_0(u_alu_result), .in_1(u_alu_2_result), .out(multiplexer_1_out));
  BitExtender #(.inputBits(16), .outputBits(32)) bitextender_1 (.in(cpumemory_d2), .out(SignExt));
  alu_control #(.applicationType("IVERILOG"), .CodeFile(".\\alu_control.v")) u_alu_control (
    .alu_op(ALUop), .funct(cpumemory_d2[5:0]), .alu_control(u_alu_control_alu_control));
  Multiplexer #(.Bits(5)) multiplexer_2 (.sel(RegDst), .in_0(src2__addr), .in_1(cpumemory_d2[15:11]), .out(dst__addr));
  control_unit #(.applicationType("IVERILOG"), .CodeFile(".\\control_unit.v")) u_control_unit (
    .instr_op(opcode), .reg_dst(RegDst), .branch(branch), .mem_read(MemRead), .mem_to_reg(Mem2Reg),
    .alu_op(ALUop), .mem_write(MemWrite), .alu_src(ALUsrc), .reg_write(RegWrite));
  cpu_registers #(.applicationType("IVERILOG"), .CodeFile(".\\cpu_registers.v")) u_cpu_registers (
    .clk(clk), .rst(rst), .write_en(RegWrite), .src1_addr(src1__addr), .src2_addr(src2__addr),
    .dst_addr(dst__addr), .data_in(dst__data), .src1_out(src1__out), .src2_out(src2__out));
  Multiplexer #(.Bits(32)) multiplexer_3 (.sel(ALUsrc), .in_0(src2__out), .in_1(SignExt), .out(multiplexer_3_out));
  alu #(.applicationType("IVERILOG"), .CodeFile(".\\alu.v")) u_alu_3 (
    .alu_control(u_alu_control_alu_control), .A(src1__out), .B(multiplexer_3_out), .zero(zero),
    .result(ALUresult));
  Multiplexer #(.Bits(32)) multiplexer_4 (.sel(Mem2Reg), .in_0(ALUresult), .in_1(_1D), .out(dst__data));
  // Pins of 1 and 2 bits meet at {undriven[1], 1'b0}

  // Other names for the same wires on the sheet: src2Add[4:0] = src2__addr; src1Add[4:0] = src1__addr;
  //   DstAddr[4:0] = dst__addr; mux3[31:0] = dst__data; src1Out[31:0] = src1__out; src2Out[31:0] = src2__out

  // Notes on the sheet:
  //   Inputs
  //   PC
  //   Outputs for testing
endmodule
